# Fritzing sketch pico_turtle_plotter (saved by Fritzing 1.0.4)
breadboards: 1

parts:
  Pico_H1 = Raspberry Pi Pico H
  J1 = Basic Servo
  SM1 = 28BYJ-48 Stepper Motor [part_number=28BYJ-48]  # not connected
  Driver1 = 28BYJ-48 Driver Module [part_number=ULN2003 package=THT]
  SM2 = 28BYJ-48 Stepper Motor [part_number=28BYJ-48]  # not connected
  Driver2 = 28BYJ-48 Driver Module [part_number=ULN2003 package=THT]

nets:
  N1: Pico_H1.VSYS, J1.vcc, Driver1.Vmotor, Driver2.Vmotor
  GND: Pico_H1.GND, J1.gnd, Driver1.GND, Driver2.IN1, Driver2.GND
  N2: Pico_H1.GP15, J1.pulse
  N3: Pico_H1.GP8, Driver2.IN4
  N4: Pico_H1.GP7, Driver2.IN3
  N5: Pico_H1.GP6, Driver2.IN2
  N6: Pico_H1.GP4, Driver1.IN4
  N7: Pico_H1.GP3, Driver1.IN3
  N8: Pico_H1.GP1, Driver1.IN2
  N9: Pico_H1.GP0, Driver1.IN1

custom parts:
  Raspberry Pi Pico H: Raspberry Pi Pico H. Based around the RP2040 microcontroller the Pico H is a low cost microcontroller device bringing Raspberry Pi quality, cost, and easy of use to the microcontroller space.
  28BYJ-48 Stepper Motor: Unipolar Stepper Motor 28BYJ-48 Top coil - pink & orange Bottom coil - blue & yellow Common rail - red Connector pins: blue - pink - yellow - orange - red
  28BYJ-48 Driver Module: ULN2003 Driver Module for the 28BYJ-48 Unipolar Stepper Motor LED A - Blue wire - Bottom coil left LED B - Pink wire - Top coil left LED C - Yellow wire - Bottom coil right LED D - Orange wire - Top coil right Common rail - red Connector pins: blue - pink - yellow - orange - red Control pins - IN1 to IN4 Power pins - GND & Vmotor (5-12V) On/Off jumper (if removed, power to motor is cut).
